# Fritzing sketch IR_arduino (saved by Fritzing 0.9.3b)

parts:
  Power_5_5x2_1 = Power 5.5x2.5
  IR1 = TSOP312.., 314.. [package=THT]
  Часть1 = Arduino Nano (Rev3.0)

nets:
  N1: Power_5_5x2_1.PWR, Часть1.5V
  GND: Power_5_5x2_1.GND, Часть1.GND
  N2: IR1.GND, Часть1.D2
